# Fritzing sketch tasmota_window_actuator (saved by Fritzing 1.0.2b)
breadboards: 1

parts:
  Relay_1 = Inductor [package="0603 [SMD]"]
  Relay_2 = SPST Switch [package=switch-spdt_lock.007s]
  IC1 = WeMos D1 Mini
  5v = generic-ac-power-supply [package=THT]
  part = AC Power [voltage=220 frequency=50]
  Fuse = FUSE [package=fuse_5mm]
  Varistor = V18ZA2P [package=v18za2p]
  12v = generic-ac-power-supply [package=THT]
  Relay_1_2 = SPST Switch [package=switch-spdt_lock.007s]
  Relay_3 = SPST Switch [package=switch-spdt_lock.007s]
  Relay_4 = SPST Switch [package=switch-spdt_lock.007s]
  M1 = DC Motor [voltage_(max)=6V voltage_(min)=3V]
  8_x_RGB_LED = ws2812b [package="smd 2812b"]
  2_8 = ws2812b [package="smd 2812b"]
  Relay_2_2 = Inductor [package="0603 [SMD]"]
  Relay_4_2 = Inductor [package="0603 [SMD]"]
  Relay_3_2 = Inductor [package="0603 [SMD]"]
  OPEN = Round Pushbutton
  part_2 = Resistor [tolerance=±5% power=0.25W resistance=4,.7k package=THT]
  CLOSE = Round Pushbutton
  part_3 = Resistor [tolerance=±5% power=0.25W resistance=4,.7k package=THT]

nets:
  N1: Relay_1.pin_0, IC1.D1, Relay_2_2.pin_0
  GND: Relay_1.pin_1, IC1.G, 5v.pin3#2, 8_x_RGB_LED.VSS, 2_8.VSS, Relay_2_2.pin_1, Relay_4_2.pin_1, Relay_3_2.pin_1, part_2.Pin_1, part_3.Pin_1
  N2: Relay_2.P, Relay_4.P
  N3: Relay_2.S, M1.pin_2
  3.3V: IC1.3V3, OPEN.leg0, CLOSE.leg0
  5V: IC1.5V, 5v.pin3#3, 8_x_RGB_LED.VDD, 2_8.VDD
  N4: IC1.D2, Relay_4_2.pin_0, Relay_3_2.pin_0
  N5: IC1.D4, 8_x_RGB_LED.DIN
  N6: IC1.D6, OPEN.leg1, part_2.Pin_0
  N7: IC1.D7, CLOSE.leg1, part_3.Pin_0
  N8: 5v.pin1, Fuse.2, Varistor.P$1, Relay_1_2.P
  N9: 5v.pin2, part.V-, Varistor.P$2, 12v.pin2
  N10: part.V+, Fuse.1
  N11: 12v.pin1, Relay_1_2.S
  N12: 12v.pin3#2, Relay_3.S, Relay_4.O
  N13: 12v.pin3#3, Relay_3.O, Relay_4.S
  N14: Relay_3.P, M1.pin_1
  N15: 8_x_RGB_LED.DOUT, 2_8.DIN

custom parts:
  generic-ac-power-supply: Generic ac power supply module. Use as is, or customize the svgs to fit your particular device (as they are all different.) Provides AC input and single DC output. PCB is generic and will need modifications if you intend to do a pcb mount.
